// Logisim project Regfile.circ as structural Verilog: 1 circuit, main circuit main
module main (
  input  [1:0] Read_register_1,
  input  [1:0] Read_register_2,
  input  [1:0] write_register,
  input  [15:0] write_data,
  input  RegWrite,
  input  clock,
  output [15:0] Reg_0_Value,
  output [15:0] Reg_1_Value,
  output [15:0] Reg_2_Value,
  output [15:0] Reg_3_Value,
  output [15:0] Read_Data_1,
  output [15:0] Read_Data_2
);

  wire w0, w1, w2, w3;
  wire [1:0] subtractor_1_out, subtractor_2_out, subtractor_3_out, subtractor_4_out;
  wire [15:0] in0, in1, in2, in3;

  Register #(.width(16)) Reg_0 (.D(in0), .en(w0), .Q(Reg_0_Value), .clk(clock));  // open: clr
  Register #(.width(16)) Reg_1 (.D(in1), .en(w1), .Q(Reg_1_Value), .clk(clock));  // open: clr
  Subtractor #(.width(2)) subtractor_1 (.a(2'b00), .b(write_register), .out(subtractor_1_out));  // open: bin, bout
  Subtractor #(.width(2)) subtractor_2 (.a(2'b01), .b(write_register), .out(subtractor_2_out));  // open: bin, bout
  Subtractor #(.width(2)) subtractor_3 (.a(2'b10), .b(write_register), .out(subtractor_3_out));  // open: bin, bout
  Subtractor #(.width(2)) subtractor_4 (.a(2'b11), .b(write_register), .out(subtractor_4_out));  // open: bin, bout
  Register #(.width(16)) reg_2 (.D(in2), .en(w2), .Q(Reg_2_Value), .clk(clock));  // open: clr
  Comparator #(.width(2)) comparator_1 (.a(subtractor_1_out), .b(2'b00), .eq(w0));  // open: gt, lt
  Comparator #(.width(2)) comparator_2 (.a(subtractor_2_out), .b(2'b00), .eq(w1));  // open: gt, lt
  Comparator #(.width(2)) comparator_3 (.a(subtractor_3_out), .b(2'b00), .eq(w2));  // open: gt, lt
  Comparator #(.width(2)) comparator_4 (.a(subtractor_4_out), .b(2'b00), .eq(w3));  // open: gt, lt
  Register #(.width(16)) Reg_3 (.D(in3), .en(w3), .Q(Reg_3_Value), .clk(clock));  // open: clr
  Multiplexer #(.select(2), .width(16)) multiplexer_1 (
    .in0(Reg_0_Value), .in1(Reg_1_Value), .in2(Reg_2_Value), .in3(Reg_3_Value), .out(Read_Data_1),
    .sel(Read_register_1));  // open: en
  Multiplexer #(.select(2), .width(16)) multiplexer_2 (
    .in0(Reg_0_Value), .in1(Reg_1_Value), .in2(Reg_2_Value), .in3(Reg_3_Value), .out(Read_Data_2),
    .sel(Read_register_2));  // open: en
  Demultiplexer #(.select(2), .width(16)) demultiplexer_1 (
    .out0(in0), .out1(in1), .out2(in2), .out3(in3), .in(write_data), .sel(write_register), .en(RegWrite));

  // Other names for the same wires on the sheet: clk = clock; r0v[15:0] = Reg_0_Value; r1v[15:0] = Reg_1_Value;
  //   r2v[15:0] = Reg_2_Value; r3v[15:0] = Reg_3_Value; rr1[1:0] = Read_register_1; rr2[1:0] = Read_register_2;
  //   rw = RegWrite; wd[15:0] = write_data; wr[1:0] = write_register

  // Notes on the sheet:
  //   These are INPUTS to the circuit
  //   These are INPUTS to the circuit
  //   DO NOT CHANGE THE LOCATIONS OF THE INPUTS/OUTPUTS! IF YOU DO SO, YOU NEED TO MAKE SURE THE PINS ARE AT THE RIGHT PLACE!
  //   These are OUTPUTS to the circuit
  //   Yet again, the clock is not an actual clock, but an input, one that will be driven from a higher circuit
  //   These are OUTPUTS to the circuit
endmodule
