// Logisim project alu.circ as structural Verilog: 3 circuits, main circuit main
module main (
  input  [15:0] X,
  input  [15:0] Y,
  input  [3:0] Switch__S,
  output Signed_Overflow,
  output [15:0] RESULT,
  output Equal
);

  all_ops all_ops_1 (.X(X), .Y(Y), .Switch__S(Switch__S), .overflow(Signed_Overflow), .out(RESULT));
  Comparator #(.width(16)) comparator_1 (.a(X), .b(Y), .eq(Equal));  // open: gt, lt

  // Notes on the sheet:
  //   INPUTS to your circuit
  //   INPUT to your circuit
  //   DON'T CHANGE THE INPUTS AND OUTPUTS! IF YOU DO SO, YOU NEED TO MAKE SURE THE PINS ARE IN THE RIGHT PLACES!
  //   OUTPUTS of your circuit
endmodule

module all_ops (
  input  [15:0] X,
  input  [15:0] Y,
  input  [3:0] Switch__S,
  output overflow,
  output [15:0] out
);

  wire comparator_1_lt, oadd, oadd8, osub, osub8, overflow_3_overflow, overflow_4_overflow,
       overflow_5_overflow, overflow_6_overflow;
  wire [15:0] add, addp8, \and , bit_extender_1_out, bit_extender_2_out, bit_extender_3_out,
       bit_extender_4_out, bit_extender_6_out, bit_extender_7_out, bit_extender_8_out, bit_extender_9_out,
       lui, \or , sllv, slt, srav, srlv, sub, subp8;

  assign bit_extender_1_out = {{8{X[7]}}, X[7:0]};  // Bit_Extender bit_extender_1
  assign bit_extender_2_out = {{8{X[15]}}, X[15:8]};  // Bit_Extender bit_extender_2
  assign bit_extender_3_out = {{8{Y[7]}}, Y[7:0]};  // Bit_Extender bit_extender_3
  assign bit_extender_4_out = {{8{Y[15]}}, Y[15:8]};  // Bit_Extender bit_extender_4
  Adder #(.width(16)) adder_1 (.a(X), .b(Y), .out(add));  // open: cin, cout
  Shifter #(.width(16), .shift("lr")) shifter_1 (.in(X), .\dist (Y[3:0]), .out(srlv));
  Comparator #(.width(16)) comparator_1 (.a(X), .b(Y), .lt(comparator_1_lt));  // open: gt, eq
  assign \and  = X & Y;  // AND_Gate and_1, 16 bits wide
  Adder adder_2 (.a(X[7:0]), .b(Y[7:0]), .out(addp8[7:0]));  // open: cin, cout
  Adder adder_3 (.a(X[15:8]), .b(Y[15:8]), .out(addp8[15:8]));  // open: cin, cout
  Shifter #(.width(16)) shifter_2 (.in(Y), .\dist (4'b1000), .out(lui));
  overflow overflow_1 (.result(out), .X(X), .Y(Y), .add_sub(2'b01), .overflow(oadd));
  overflow overflow_2 (.result(out), .X(X), .Y(Y), .add_sub(2'b00), .overflow(osub));
  overflow overflow_3 (
    .result(out), .X(bit_extender_1_out), .Y(bit_extender_3_out), .add_sub(2'b01),
    .overflow(overflow_3_overflow));
  overflow overflow_4 (
    .result(out), .X(bit_extender_2_out), .Y(bit_extender_4_out), .add_sub(2'b01),
    .overflow(overflow_4_overflow));
  assign slt = {{15{1'b0}}, comparator_1_lt};  // Bit_Extender bit_extender_5
  or or_1 (oadd8, overflow_3_overflow, overflow_4_overflow);
  Subtractor #(.width(16)) subtractor_1 (.a(X), .b(Y), .out(sub));  // open: bin, bout
  Shifter #(.width(16), .shift("ar")) shifter_3 (.in(X), .\dist (Y[3:0]), .out(srav));
  assign \or  = X | Y;  // OR_Gate or_2, 16 bits wide
  Subtractor subtractor_2 (.a(X[7:0]), .b(Y[7:0]), .out(subp8[7:0]));  // open: bin, bout
  Subtractor subtractor_3 (.a(X[15:8]), .b(Y[15:8]), .out(subp8[15:8]));  // open: bin, bout
  assign bit_extender_6_out = {{8{X[7]}}, X[7:0]};  // Bit_Extender bit_extender_6
  assign bit_extender_7_out = {{8{X[15]}}, X[15:8]};  // Bit_Extender bit_extender_7
  Shifter #(.width(16)) shifter_4 (.in(X), .\dist (Y[3:0]), .out(sllv));
  assign bit_extender_8_out = {{8{Y[7]}}, Y[7:0]};  // Bit_Extender bit_extender_8
  assign bit_extender_9_out = {{8{Y[15]}}, Y[15:8]};  // Bit_Extender bit_extender_9
  overflow overflow_5 (
    .result(out), .X(bit_extender_6_out), .Y(bit_extender_8_out), .add_sub(2'b00),
    .overflow(overflow_5_overflow));
  or or_3 (osub8, overflow_5_overflow, overflow_6_overflow);
  overflow overflow_6 (
    .result(out), .X(bit_extender_7_out), .Y(bit_extender_9_out), .add_sub(2'b00),
    .overflow(overflow_6_overflow));
  Multiplexer #(.select(4)) multiplexer_1 (
    .in0(oadd), .in1(osub), .in2(1'b0), .in3(1'b0), .in4(1'b0), .in5(1'b0), .in6(1'b0), .in7(1'b0),
    .in8(1'b0), .in9(oadd8), .in10(osub8), .in11(1'b0), .out(overflow), .sel(Switch__S));  // open: in12, in13, in14, in15, en
  Multiplexer #(.select(4), .width(16)) multiplexer_2 (
    .in0(add), .in1(sub), .in2(sllv), .in3(srlv), .in4(srav), .in5(slt), .in6(\or ), .in7(\and ),
    .in8(addp8), .in9(addp8), .in10(lui), .out(out), .sel(Switch__S));  // open: in11, in12, in13, in14, in15, en

  // Other names for the same wires on the sheet: result[15:0] = out; switch[3:0] = Switch__S; _07x[7:0] = X[7:0];
  //   _815x[7:0] = X[15:8]; _07y[7:0] = Y[7:0]; _815y[7:0] = Y[15:8]
endmodule

module overflow (
  input  [15:0] result,
  input  [15:0] X,
  input  [15:0] Y,
  input  [1:0] add_sub,
  output overflow
);

  wire comparator_1_eq, comparator_2_gt, comparator_3_eq, comparator_4_eq, comparator_5_lt, comparator_6_gt,
       comparator_7_gt, comparator_8_lt, comparator_9_lt, comparator_10_gt, comparator_11_eq,
       comparator_12_eq, comparator_13_gt, comparator_14_lt, comparator_15_gt, comparator_16_eq,
       comparator_17_lt, comparator_18_lt, o1, o2, o3, o4, or_1_out, or_2_out;

  Comparator #(.width(2)) comparator_1 (.a(add_sub), .b(2'b00), .eq(comparator_1_eq));  // open: gt, lt
  Comparator #(.width(16)) comparator_2 (.a(result), .b({16{1'b0}}), .gt(comparator_2_gt));  // open: eq, lt
  Comparator #(.width(16)) comparator_3 (.a(result), .b({16{1'b0}}), .eq(comparator_3_eq));  // open: gt, lt
  Comparator #(.width(2)) comparator_4 (.a(add_sub), .b(2'b00), .eq(comparator_4_eq));  // open: gt, lt
  Comparator #(.width(16)) comparator_5 (.a(result), .b({16{1'b0}}), .lt(comparator_5_lt));  // open: gt, eq
  Comparator #(.width(16)) comparator_6 (.a(X), .b({16{1'b0}}), .gt(comparator_6_gt));  // open: eq, lt
  Comparator #(.width(16)) comparator_7 (.a(Y), .b({16{1'b0}}), .gt(comparator_7_gt));  // open: eq, lt
  or or_1 (or_1_out, comparator_2_gt, comparator_3_eq);
  Comparator #(.width(16)) comparator_8 (.a(X), .b({16{1'b0}}), .lt(comparator_8_lt));  // open: gt, eq
  Comparator #(.width(16)) comparator_9 (.a(Y), .b({16{1'b0}}), .lt(comparator_9_lt));  // open: gt, eq
  and and_1 (o1, comparator_4_eq, comparator_5_lt, comparator_6_gt, comparator_7_gt);
  and and_2 (o2, comparator_1_eq, or_1_out, comparator_8_lt, comparator_9_lt);
  Comparator #(.width(16)) comparator_10 (.a(X), .b({16{1'b0}}), .gt(comparator_10_gt));  // open: eq, lt
  Comparator #(.width(16)) comparator_11 (.a(X), .b({16{1'b0}}), .eq(comparator_11_eq));  // open: gt, lt
  Comparator #(.width(2)) comparator_12 (.a(add_sub), .b(2'b00), .eq(comparator_12_eq));  // open: gt, lt
  Comparator #(.width(16)) comparator_13 (.a(result), .b({16{1'b0}}), .gt(comparator_13_gt));  // open: eq, lt
  Comparator #(.width(16)) comparator_14 (.a(X), .b({16{1'b0}}), .lt(comparator_14_lt));  // open: gt, eq
  Comparator #(.width(16)) comparator_15 (.a(Y), .b({16{1'b0}}), .gt(comparator_15_gt));  // open: eq, lt
  Comparator #(.width(2)) comparator_16 (.a(add_sub), .b(2'b00), .eq(comparator_16_eq));  // open: gt, lt
  Comparator #(.width(16)) comparator_17 (.a(result), .b({16{1'b0}}), .lt(comparator_17_lt));  // open: gt, eq
  or or_2 (or_2_out, comparator_10_gt, comparator_11_eq);
  Comparator #(.width(16)) comparator_18 (.a(Y), .b({16{1'b0}}), .lt(comparator_18_lt));  // open: gt, eq
  or or_3 (overflow, o1, o2, o3, o4);
  and and_3 (o3, comparator_12_eq, comparator_13_gt, comparator_14_lt, comparator_15_gt);
  and and_4 (o4, comparator_16_eq, comparator_17_lt, or_2_out, comparator_18_lt);

  // Other names for the same wires on the sheet: as[1:0] = add_sub; res[15:0] = result

  // Notes on the sheet:
  //   10 if noflow, 01 if add, 00 if sub
endmodule
