// Logisim project cpu.circ as structural Verilog: 2 circuits, main circuit main
module main (
  input  [15:0] From_Instr_Mem,
  input  clk,
  output [15:0] r0,
  output [15:0] r1,
  output [15:0] r2,
  output [15:0] r3,
  output [15:0] Display_0,
  output [15:0] Display_1,
  output [15:0] To_Instr_Mem,
  output [15:0] Data_Mem_Data,
  output [15:0] Data_Mem_Addr,
  output Data_Mem_Write
);

  wire ALUSrc, b_taken, button_1_out, equal, ExtOp, not_1_out, or_1_out, overflow, RegWr, up_disp0, up_disp1;
  wire [1:0] nPC_sel, reg_src, RegDst, wr_reg;
  wire [3:0] ALUctr;
  wire [7:0] imm;
  wire [15:0] adder_1_out, adder_2_out, and_1_out, bit_extender_1_out, bit_extender_2_out,
       bit_extender_3_out, bit_extender_4_out, ext_imm, ind0, ind1, mem_res, multiplexer_2_out,
       multiplexer_3_out, next_instr, or_2_out, or_3_out, rs_val, subtractor_1_out, wr_dat;
  wire [15:8] instr_in;

  control control_1 (
    .instruction({instr_in, imm}), .Equal(equal), .nPC_sel(nPC_sel), .RegDst(RegDst), .ExtOp(ExtOp),
    .RegWr(RegWr), .ALUSrc(ALUSrc), .ALUctr(ALUctr), .reg_src(reg_src), .MemWr(Data_Mem_Write),
    .disp0_write(up_disp0), .disp1_write(up_disp1), .instr_in(b_taken));
  Multiplexer #(.select(2), .width(2)) multiplexer_1 (
    .in0(imm[7:6]), .in1(instr_in[9:8]), .in2(2'b11), .out(wr_reg), .sel(RegDst));  // open: in3, en
  Register #(.width(16)) currPC (.D(next_instr), .Q(To_Instr_Mem), .clk(clk));  // open: en, clr
  Demultiplexer #(.width(16)) demultiplexer_1 (.out0(ind0), .out1(ind1), .in(rs_val), .sel(imm[0]), .en(or_1_out));
  or or_1 (or_1_out, up_disp0, up_disp1);
  Multiplexer #(.width(16)) multiplexer_2 (
    .in0(From_Instr_Mem), .in1(16'h6), .out(multiplexer_2_out), .sel(b_taken));  // open: en
  Multiplexer #(.width(16)) multiplexer_3 (
    .in0(ext_imm), .in1(Data_Mem_Data), .out(multiplexer_3_out), .sel(ALUSrc));  // open: en
  Regfile_main main_1 (
    .Read_register_1(instr_in[11:10]), .Read_register_2(instr_in[9:8]), .write_register(wr_reg),
    .write_data(wr_dat), .Reg_0_Value(r0), .Reg_1_Value(r1), .Reg_2_Value(r2), .Reg_3_Value(r3),
    .RegWrite(RegWr), .clock(clk), .Read_Data_1(rs_val), .Read_Data_2(Data_Mem_Data));
  alu_main main_2 (
    .Switch__S(ALUctr), .X(rs_val), .Equal(equal), .RESULT(Data_Mem_Addr), .Signed_Overflow(overflow),
    .Y(multiplexer_3_out));
  Register #(.width(16)) register_1 (.D(multiplexer_2_out), .Q({instr_in, imm}), .clk(clk));  // open: en, clr
  assign bit_extender_1_out = {{8{1'b0}}, imm};  // Bit_Extender bit_extender_1
  Multiplexer #(.width(16)) multiplexer_4 (
    .in0(bit_extender_1_out), .in1(bit_extender_2_out), .out(ext_imm), .sel(ExtOp));  // open: en
  assign bit_extender_2_out = {{8{imm[7]}}, imm};  // Bit_Extender bit_extender_2
  Multiplexer #(.select(2), .width(16)) multiplexer_5 (
    .in0(Data_Mem_Addr), .in1(mem_res), .in2(To_Instr_Mem), .out(wr_dat), .sel(reg_src));  // open: in3, en
  Subtractor #(.width(16)) subtractor_1 (.a(To_Instr_Mem), .b(16'h1), .out(subtractor_1_out));  // open: bin, bout
  Hex_Digit_Display hex_digit_display_1 (.value(Display_0[15:12]));  // open: dp
  Register #(.width(16)) disp0val (.D(ind0), .en(up_disp0), .Q(Display_0), .clk(clk));  // open: clr
  assign bit_extender_3_out = {{8{imm[7]}}, imm};  // Bit_Extender bit_extender_3
  assign bit_extender_4_out = {{4{1'b0}}, {instr_in[11:8], imm}};  // Bit_Extender bit_extender_4
  assign and_1_out = subtractor_1_out & 16'hf000;  // AND_Gate and_1, 16 bits wide
  not not_1 (not_1_out, Data_Mem_Write);
  Hex_Digit_Display hex_digit_display_2 (.value(Display_0[11:8]));  // open: dp
  Hex_Digit_Display hex_digit_display_3 (.value(Display_0[7:4]));  // open: dp
  assign mem_res = Data_Mem_Write ? Data_Mem_Data : 16'bz;  // Controlled_Buffer controlled_buffer_1
  RAM #(.addrWidth(16), .dataWidth(16)) ram_1 (
    .addr(Data_Mem_Addr), .data(mem_res), .sel(1'b1), .clk(clk), .ld(not_1_out), .clr(button_1_out));
  Button button_1 (.out(button_1_out));
  Hex_Digit_Display hex_digit_display_4 (.value(Display_0[3:0]));  // open: dp
  Hex_Digit_Display hex_digit_display_5 (.value(Display_1[15:12]));  // open: dp
  Register #(.width(16)) disp1val (.D(ind1), .en(up_disp1), .Q(Display_1), .clk(clk));  // open: clr
  Adder #(.width(16)) adder_1 (.a(To_Instr_Mem), .b(16'h1), .out(adder_1_out));  // open: cin, cout
  Adder #(.width(16)) adder_2 (.a(To_Instr_Mem), .b(bit_extender_3_out), .out(adder_2_out));  // open: cin, cout
  assign or_2_out = bit_extender_4_out | and_1_out;  // OR_Gate or_2, 16 bits wide
  assign or_3_out = and_1_out | rs_val;  // OR_Gate or_3, 16 bits wide
  LED led_1 (.in(overflow));
  Hex_Digit_Display hex_digit_display_6 (.value(Display_1[11:8]));  // open: dp
  Hex_Digit_Display hex_digit_display_7 (.value(Display_1[7:4]));  // open: dp
  Multiplexer #(.select(2), .width(16)) multiplexer_6 (
    .in0(adder_1_out), .in1(adder_2_out), .in2(or_2_out), .in3(or_3_out), .out(next_instr), .sel(nPC_sel));  // open: en
  Hex_Digit_Display hex_digit_display_8 (.value(Display_1[3:0]));  // open: dp

  // Other names for the same wires on the sheet: alu_res[15:0] = Data_Mem_Addr; currPC[15:0] = To_Instr_Mem;
  //   d0[15:0] = Display_0; d1[15:0] = Display_1; instr_in[7:0] = imm; tar_addr[11:0] = {instr_in[11:8], imm};
  //   rd[1:0] = imm[7:6]; rt[1:0] = instr_in[9:8]; rs[1:0] = instr_in[11:10]; MemWr = Data_Mem_Write;
  //   rt_val[15:0] = Data_Mem_Data

  // Notes on the sheet:
  //   control
  //   which register will be written to
  //   choose display
  //   This is the current PC that you need to send as OUTPUT
  //   This is the instruction that you would receive as INPUT
  //   branch killing
  //   This is a CLK that is an INPUT driven from the harness.
  //   Remember, this circuit is loaded from the harness to be tested!
  //   DO NOT CHANGE THE LOCATIONS OF THE INPUTS OR OUTPUTS! IF YOU DO SO, YOU NEED TO MAKE SURE THE PINS ARE IN THE RIGHT PLACES!
  //   RegFile
  //   ALU
  //   immediate extension
  //   breakdown instruction
  //   Choose Register Data Source
  //   These are OUTPUTS of the circuit
  //   memory
  //   display 0
  //   display 1
  //   Instruction Selection
  //   These are OUTPUTS of the circuit
endmodule

module control (
  input  [15:0] instruction,
  input  Equal,
  output [1:0] nPC_sel,
  output [1:0] RegDst,
  output ExtOp,
  output RegWr,
  output ALUSrc,
  output [3:0] ALUctr,
  output [1:0] reg_src,
  output MemWr,
  output disp0_write,
  output disp1_write,
  output instr_in
);

  wire comparator_1_eq, comparator_2_eq, comparator_5_eq, comparator_6_eq, isR, not_1_out;
  wire [1:0] eq, neq;
  wire [3:0] aluop;

  Comparator #(.width(2)) comparator_1 (.a(instruction[1:0]), .b(2'b00), .eq(comparator_1_eq));  // open: gt, lt
  Comparator #(.width(4)) comparator_2 (.a(instruction[15:12]), .b(4'b1100), .eq(comparator_2_eq));  // open: gt, lt
  Comparator #(.width(2), .mode("unsigned")) comparator_3 (.a(nPC_sel), .b(2'b00), .gt(instr_in));  // open: eq, lt
  assign eq = {{1{1'b0}}, Equal};  // Bit_Extender bit_extender_1
  not not_1 (not_1_out, Equal);
  assign neq = {{1{1'b0}}, not_1_out};  // Bit_Extender bit_extender_2
  Multiplexer #(.select(4), .width(2), .enable("false")) multiplexer_1 (
    .in0(2'b00), .in1(2'b10), .in2(2'b00), .in3(2'b00), .in4(2'b00), .in5(2'b00), .in6(2'b00), .in7(2'b00),
    .in8(2'b00), .in9(2'b01), .in10(2'b00), .in11(2'b01), .in12(2'b00), .out(reg_src),
    .sel(instruction[15:12]));  // open: in13, in14, in15
  Multiplexer #(.select(4), .enable("false")) multiplexer_2 (
    .in0(1'b0), .in1(1'b0), .in2(1'b0), .in3(1'b0), .in4(1'b0), .in5(1'b0), .in6(1'b0), .in7(1'b0),
    .in8(1'b0), .in9(1'b1), .in10(1'b0), .in11(1'b0), .in12(1'b0), .out(MemWr), .sel(instruction[15:12]));  // open: in13, in14, in15
  and and_1 (disp0_write, comparator_1_eq, comparator_2_eq);
  Comparator #(.width(4)) comparator_4 (.a(instruction[15:12]), .b(4'b0000), .eq(isR));  // open: gt, lt
  Multiplexer #(.select(4), .enable("false")) multiplexer_3 (
    .in0(1'b0), .in1(1'b0), .in2(1'b0), .in3(1'b0), .in4(1'b1), .in5(1'b1), .in6(1'b0), .in7(1'b0),
    .in8(1'b1), .in9(1'b1), .in10(1'b0), .in11(1'b1), .in12(1'b0), .out(ExtOp), .sel(instruction[15:12]));  // open: in13, in14, in15
  Multiplexer #(.select(4), .enable("false")) multiplexer_4 (
    .in0(1'b1), .in1(1'b0), .in2(1'b0), .in3(1'b0), .in4(1'b1), .in5(1'b0), .in6(1'b0), .in7(1'b0),
    .in8(1'b1), .in9(1'b0), .in10(1'b0), .in11(1'b0), .in12(1'b0), .out(ALUSrc), .sel(instruction[15:12]));  // open: in13, in14, in15
  Comparator #(.width(2)) comparator_5 (.a(instruction[1:0]), .b(2'b01), .eq(comparator_5_eq));  // open: gt, lt
  Comparator #(.width(4)) comparator_6 (.a(instruction[15:12]), .b(4'b1100), .eq(comparator_6_eq));  // open: gt, lt
  Multiplexer #(.width(4), .enable("false")) multiplexer_5 (
    .in0(aluop), .in1(instruction[3:0]), .sel(isR));  // open: out
  and and_2 (disp1_write, comparator_5_eq, comparator_6_eq);
  Multiplexer #(.select(4), .enable("false")) multiplexer_6 (
    .in0(1'b1), .in1(1'b1), .in2(1'b0), .in3(1'b0), .in4(1'b0), .in5(1'b1), .in6(1'b1), .in7(1'b1),
    .in8(1'b0), .in9(1'b0), .in10(1'b1), .in11(1'b1), .in12(1'b0), .out(RegWr), .sel(instruction[15:12]));  // open: in13, in14, in15
  Multiplexer #(.select(4), .width(4), .enable("false")) multiplexer_7 (
    .in0(instruction[3:0]), .in1(4'b1111), .in2(4'b1111), .in3(4'b1111), .in4(4'b1111), .in5(4'b0000),
    .in6(4'b0111), .in7(4'b0110), .in8(4'b1111), .in9(4'b0000), .in10(4'b1010), .in11(4'b0000),
    .in12(4'b1111), .out(ALUctr), .sel(instruction[15:12]));  // open: in13, in14, in15
  Multiplexer #(.select(4), .width(2), .enable("false")) multiplexer_8 (
    .in0(2'b00), .in1(2'b10), .in2(2'b10), .in3(2'b11), .in4(eq), .in5(2'b00), .in6(2'b00), .in7(2'b00),
    .in8(neq), .in9(2'b00), .in10(2'b00), .in11(2'b00), .in12(2'b00), .out(nPC_sel), .sel(instruction[15:12]));  // open: in13, in14, in15
  Multiplexer #(.select(4), .width(2), .enable("false")) multiplexer_9 (
    .in0(2'b00), .in1(2'b10), .in2(2'b11), .in3(2'b11), .in4(2'b11), .in5(2'b01), .in6(2'b01), .in7(2'b01),
    .in8(2'b11), .in9(2'b11), .in10(2'b01), .in11(2'b01), .in12(2'b11), .out(RegDst), .sel(instruction[15:12]));  // open: in13, in14, in15

  // Other names for the same wires on the sheet: ac[3:0] = ALUctr; as = ALUSrc; b_taken = instr_in; d0w = disp0_write;
  //   d1w = disp1_write; eo = ExtOp; func[5:0] = instruction[5:0]; ins[15:0] = instruction;
  //   op[3:0] = instruction[15:12]; mw = MemWr; nps[1:0] = nPC_sel; r_src[1:0] = reg_src; rdst[1:0] = RegDst;
  //   rw = RegWr

  // Notes on the sheet:
  //   Determine reg_src
  //   Determine MemWr
  //   Determine disp0_write
  //   Determine ExtOp
  //   Determine ALUSrc
  //   Determine disp0_write
  //   Determine RegWr
  //   Determine ALUctr
  //   Determine nPC_set
  //   Determine RegDst
  //   00 if PC+1, 01 if branch
  //   10 if jump, 11 if jr
  //   00 if rd, 01 if rt, 10 if r3
  //   Low if zero, high if sign
  //   High if register, low if immediate
  //   01 if memory, 00 if alu, 10 if PC
endmodule
